// Logisim project cpu.circ as structural Verilog: 7 circuits, main circuit main
module main (
  input  [31:0] INSTRUCTION,
  input  CLOCK,
  output [31:0] PROGRAM_COUNTER,
  output [31:0] ra,
  output [31:0] sp,
  output [31:0] t0,
  output [31:0] t1,
  output [31:0] t2,
  output [31:0] s0,
  output [31:0] s1,
  output [31:0] a0
);

  wire ASel, BrEq, BrLT, BrUn, BSel, MemRW, PCSel, RegWEn;
  wire [1:0] WBSel;
  wire [2:0] ImmSel;
  wire [3:0] ALUSel;
  wire [4:0] rd, rs1, rs2;
  wire [31:0] ALUOut, imm, instID, MemData, multiplexer_1_out, multiplexer_2_out, multiplexer_3_out, PCPlus4,
       rs1Out, rs2Out, wb;

  Adder #(.width(32)) adder_1 (.a(PROGRAM_COUNTER), .b(32'h4), .out(PCPlus4));  // open: cin, cout
  Register #(.width(32)) register_1 (.D(INSTRUCTION), .clk(CLOCK), .Q(instID));  // open: en, clr
  Multiplexer #(.width(32), .enable("false")) multiplexer_1 (
    .in0(PCPlus4), .in1(ALUOut), .out(multiplexer_1_out), .sel(PCSel));
  Register #(.width(32)) PC (.D(multiplexer_1_out), .clk(CLOCK), .Q(PROGRAM_COUNTER));  // open: en, clr
  Decodery decodery_1 (
    .Instruction(instID), .rd(rd), .rs1(rs1), .rs2(rs2));  // open: opcode, funct3, funct7, immI, immS, immB, immU, immJ
  ImmGen immgen_1 (.Instruction(instID), .ImmSel(ImmSel), .clk(CLOCK), .imm(imm));
  regfile_main RegFile (
    .rs2(rs2), .rd(rd), .Read_Data_1(rs1Out), .Read_Data_2(rs2Out), .ra(ra), .sp(sp), .t0(t0), .t1(t1),
    .t2(t2), .s0(s0), .s1(s1), .a0(a0), .rs1(rs1), .Write_Data(wb), .RegWEn(RegWEn), .clk(CLOCK));
  BrCmp brcmp_1 (.rs1(rs1Out), .rs2(rs2Out), .BrUn(BrUn), .BrEq(BrEq), .BrLt(BrLT));
  Multiplexer #(.width(32), .enable("false")) multiplexer_2 (
    .in0(rs1Out), .in1(PROGRAM_COUNTER), .out(multiplexer_2_out), .sel(ASel));
  Multiplexer #(.width(32), .enable("false")) multiplexer_3 (
    .in0(rs2Out), .in1(imm), .out(multiplexer_3_out), .sel(BSel));
  Control control_1 (
    .Instruction(INSTRUCTION), .BrEq(BrEq), .BrLt(BrLT), .PCSel(PCSel), .RegWEn(RegWEn), .ImmSel(ImmSel),
    .BrUn(BrUn), .BSel(BSel), .ASel(ASel), .ALUSel(ALUSel), .MemRW(MemRW), .WBSel(WBSel));
  alu alu_1 (.B(multiplexer_3_out), .Result(ALUOut), .A(multiplexer_2_out), .ALUSel(ALUSel));
  Multiplexer #(.select(2), .width(32), .enable("false")) multiplexer_4 (
    .in0(PCPlus4), .in1(ALUOut), .in2(MemData), .out(wb), .sel(WBSel));  // open: in3
  // mem_main main_1: pin names not known; wires that end beside it: ALUOut, rs2Out, CLOCK, MemRW, MemData
  // also tied to GND on the sheet: {ASel, ImmSel[0], ImmSel[1], ImmSel[2], PCSel, WBSel[1]}
  // also tied to VCC on the sheet: {BSel, RegWEn, WBSel[0]}

  // Other names for the same wires on the sheet: clk = CLOCK

  // Notes on the sheet:
  //   Output
  //   IMEM (do **NOT** move this)
  //   Inputs
  //   Inputs/Outputs for testing. Do **NOT** move these.
endmodule

module ImmGen (
  input  [31:0] Instruction,
  input  [2:0] ImmSel,
  input  clk,
  output [31:0] imm
);

  wire [11:0] immI, immS;
  wire [12:0] immB;
  wire [20:0] immJ;
  wire [31:0] B, I, immU, J, S;

  Decodery decodery_1 (
    .Instruction(Instruction), .immI(immI), .immS(immS), .immB(immB), .immU(immU), .immJ(immJ));  // open: opcode, rd, rs1, rs2, funct3, funct7
  assign I = {{20{immI[11]}}, immI};  // Bit_Extender bit_extender_1
  assign S = {{20{immS[11]}}, immS};  // Bit_Extender bit_extender_2
  assign B = {{19{immB[12]}}, immB};  // Bit_Extender bit_extender_3
  assign J = {{11{immJ[20]}}, immJ};  // Bit_Extender bit_extender_4
  Multiplexer #(.select(3), .width(32), .enable("false")) multiplexer_1 (
    .in0(I), .in1(S), .in2(B), .in3(immU), .in4(J), .out(imm), .sel(ImmSel));  // open: in5, in6, in7

  // Other names for the same wires on the sheet: inst[31:0] = Instruction
endmodule

module Decodery (
  input  [31:0] Instruction,
  output [6:0] opcode,
  output [4:0] rd,
  output [4:0] rs1,
  output [4:0] rs2,
  output [2:0] funct3,
  output [6:0] funct7,
  output [11:0] immI,
  output [11:0] immS,
  output [12:0] immB,
  output [31:0] immU,
  output [20:0] immJ
);


  assign funct3 = Instruction[14:12];
  assign funct7 = Instruction[31:25];
  assign immB = {Instruction[31], Instruction[7], Instruction[30:25], Instruction[11:8], 1'b0};
  assign immI = Instruction[31:20];
  assign immJ = {Instruction[31], Instruction[19:12], Instruction[20], Instruction[30:21], 1'b0};
  assign immS = {Instruction[31:25], Instruction[11:7]};
  assign immU = {Instruction[31:12], {12{1'b0}}};
  assign opcode = Instruction[6:0];
  assign rd = Instruction[11:7];
  assign rs1 = Instruction[19:15];
  assign rs2 = Instruction[24:20];

  // Other names for the same wires on the sheet: inst[31:0] = Instruction
endmodule

module Control (
  input  [31:0] Instruction,
  input  BrEq,
  input  BrLt,
  output PCSel,
  output RegWEn,
  output [2:0] ImmSel,
  output BrUn,
  output BSel,
  output ASel,
  output [3:0] ALUSel,
  output MemRW,
  output [1:0] WBSel
);

  wire not_1_out, SB_BrUn, SB_PCSel;
  wire [2:0] funct3, op1;
  wire [3:0] ALUSel_temp, op0;
  wire [4:0] op0_ext, op1_ext, sol;
  wire [6:0] funct7;

  assign op0_ext = {{1{1'b0}}, op0};  // Bit_Extender bit_extender_1
  assign op1_ext = {{2{1'b0}}, op1};  // Bit_Extender bit_extender_2
  Decodery decodery_1 (
    .Instruction(Instruction), .opcode({op1, op0}), .funct3(funct3), .funct7(funct7));  // open: rd, rs1, rs2, immI, immS, immB, immU, immJ
  Multiplexer #(.select(5), .enable("false")) multiplexer_1 (
    .in3(1'b0), .in4(1'b0), .in5(1'b0), .in6(1'b0), .in9(SB_PCSel), .in10(1'b0), .in13(1'b1), .in21(1'b1),
    .out(PCSel), .sel(sol));  // open: in0, in1, in2, in7, in8, in11, in12, in14, in15, in16, in17, in18, in19, in20, in22, in23, in24, in25, in26, in27, in28, in29, in30, in31
  Adder #(.width(5)) adder_1 (.a(op0_ext), .b(op1_ext), .out(sol));  // open: cin, cout
  Multiplexer #(.select(3), .enable("false")) multiplexer_2 ();  // open: in0, in1, in2, in3, in4, in5, in6, in7, out, sel
  Multiplexer #(.select(5), .enable("false")) multiplexer_3 (
    .in3(1'b1), .in4(1'b1), .in5(1'b0), .in6(1'b1), .in9(1'b0), .in10(1'b1), .in13(1'b1), .in21(1'b1),
    .out(RegWEn), .sel(sol));  // open: in0, in1, in2, in7, in8, in11, in12, in14, in15, in16, in17, in18, in19, in20, in22, in23, in24, in25, in26, in27, in28, in29, in30, in31
  not not_1 (not_1_out, BrEq);
  Multiplexer #(.select(3), .enable("false")) multiplexer_4 (
    .in0(BrEq), .in1(not_1_out), .in4(BrLt), .in6(BrLt), .out(SB_PCSel), .sel(funct3));  // open: in2, in3, in5, in7
  Multiplexer #(.select(5), .width(3), .enable("false")) multiplexer_5 (
    .in3(3'b000), .in4(3'b000), .in5(3'b001), .in6(3'b000), .in9(3'b010), .in10(3'b011), .in13(3'b000),
    .in21(3'b100), .out(ImmSel), .sel(sol));  // open: in0, in1, in2, in7, in8, in11, in12, in14, in15, in16, in17, in18, in19, in20, in22, in23, in24, in25, in26, in27, in28, in29, in30, in31
  Multiplexer #(.select(3), .enable("false")) multiplexer_6 (
    .in0(1'b0), .in1(1'b0), .in4(1'b0), .in6(1'b1), .out(SB_BrUn), .sel(funct3));  // open: in2, in3, in5, in7
  Multiplexer #(.select(5), .enable("false")) multiplexer_7 (
    .in3(1'b0), .in4(1'b0), .in5(1'b0), .in6(1'b0), .in9(SB_BrUn), .in10(1'b0), .in13(1'b0), .in21(1'b0),
    .out(BrUn), .sel(sol));  // open: in0, in1, in2, in7, in8, in11, in12, in14, in15, in16, in17, in18, in19, in20, in22, in23, in24, in25, in26, in27, in28, in29, in30, in31
  Multiplexer #(.select(5), .width(4), .enable("false")) multiplexer_8 (
    .in3(4'b0011), .in4(4'b0100), .in5(4'b0101), .in6(4'b0110), .in9(4'b1001), .in10(4'b1010),
    .in13(4'b1101), .in21(4'b1111), .out(ALUSel_temp), .sel(sol));  // open: in0, in1, in2, in7, in8, in11, in12, in14, in15, in16, in17, in18, in19, in20, in22, in23, in24, in25, in26, in27, in28, in29, in30, in31
  Multiplexer #(.select(5), .enable("false")) multiplexer_9 (
    .in3(1'b0), .in4(1'b0), .in5(1'b0), .in6(1'b0), .in9(1'b1), .in10(1'b0), .in13(1'b1), .in21(1'b0),
    .out(ASel), .sel(sol));  // open: in0, in1, in2, in7, in8, in11, in12, in14, in15, in16, in17, in18, in19, in20, in22, in23, in24, in25, in26, in27, in28, in29, in30, in31
  Multiplexer #(.select(5), .enable("false")) multiplexer_10 (
    .in3(1'b0), .in4(1'b0), .in5(1'b1), .in6(1'b0), .in9(1'b0), .in10(1'b0), .in13(1'b0), .in21(1'b0),
    .out(MemRW), .sel(sol));  // open: in0, in1, in2, in7, in8, in11, in12, in14, in15, in16, in17, in18, in19, in20, in22, in23, in24, in25, in26, in27, in28, in29, in30, in31
  Multiplexer #(.select(5), .enable("false")) multiplexer_11 (
    .in3(1'b1), .in4(1'b1), .in5(1'b1), .in6(1'b0), .in9(1'b1), .in10(1'b1), .in13(1'b1), .in21(1'b1),
    .out(BSel), .sel(sol));  // open: in0, in1, in2, in7, in8, in11, in12, in14, in15, in16, in17, in18, in19, in20, in22, in23, in24, in25, in26, in27, in28, in29, in30, in31
  Multiplexer #(.select(5), .width(2), .enable("false")) multiplexer_12 (
    .in3(2'b10), .in4(2'b01), .in5(2'b00), .in6(2'b01), .in9(2'b00), .in10(2'b01), .in13(2'b00),
    .in21(2'b00), .out(WBSel), .sel(sol));  // open: in0, in1, in2, in7, in8, in11, in12, in14, in15, in16, in17, in18, in19, in20, in22, in23, in24, in25, in26, in27, in28, in29, in30, in31

  // Other names for the same wires on the sheet: inst[31:0] = Instruction; opcode[6:0] = {op1, op0}
endmodule

module BrCmp (
  input  [31:0] rs1,
  input  [31:0] rs2,
  input  BrUn,
  output BrEq,
  output BrLt
);

  wire comparator_1_eq, comparator_1_lt, comparator_2_eq, comparator_2_lt;

  Comparator #(.width(32)) comparator_1 (.a(rs1), .b(rs2), .eq(comparator_1_eq), .lt(comparator_1_lt));  // open: gt
  Comparator #(.width(32), .mode("unsigned")) comparator_2 (
    .a(rs1), .b(rs2), .eq(comparator_2_eq), .lt(comparator_2_lt));  // open: gt
  Multiplexer #(.enable("false")) multiplexer_1 (.in0(comparator_1_eq), .in1(comparator_2_eq), .out(BrEq), .sel(BrUn));
  Multiplexer #(.enable("false")) multiplexer_2 (.in0(comparator_1_lt), .in1(comparator_2_lt), .out(BrLt), .sel(BrUn));

  // Other names for the same wires on the sheet: A[31:0] = rs1; B[31:0] = rs2; isUnsigned = BrUn
endmodule

module ALUSel_3 (
  input  Opcode_6,
  input  Opcode_5,
  input  Opcode_4,
  input  Opcode_3,
  input  Opcode_2,
  input  Opcode_1,
  input  Opcode_0,
  input  Funct3_2,
  input  Funct3_1,
  input  Funct3_0,
  input  Funct7_6,
  input  Funct7_5,
  input  Funct7_4,
  input  Funct7_3,
  input  Funct7_2,
  input  Funct7_1,
  input  Funct7_0,
  input  BrEq,
  input  BrLt,
  output ALUSel_3
);

  wire divu, jal, lui, mul, mulh, mulhu, remu, sub;

  and and_1 (mul, ~Opcode_6, Opcode_5, Opcode_4, ~Opcode_3, ~Opcode_2, Opcode_1, Opcode_0, ~Funct3_2, ~Funct3_1, ~Funct3_0, ~Funct7_6, ~Funct7_5, ~Funct7_4, ~Funct7_3, ~Funct7_2, ~Funct7_1, Funct7_0);  // AND_Gate
  and and_2 (sub, ~Opcode_6, Opcode_5, Opcode_4, ~Opcode_3, ~Opcode_2, Opcode_1, Opcode_0, ~Funct3_2, ~Funct3_1, ~Funct3_0, ~Funct7_6, Funct7_5, ~Funct7_4, ~Funct7_3, ~Funct7_2, ~Funct7_1, ~Funct7_0);  // AND_Gate
  and and_3 (mulh, ~Opcode_6, Opcode_5, Opcode_4, ~Opcode_3, ~Opcode_2, Opcode_1, Opcode_0, ~Funct3_2, ~Funct3_1, Funct3_0, ~Funct7_6, ~Funct7_5, ~Funct7_4, ~Funct7_3, ~Funct7_2, ~Funct7_1, Funct7_0);  // AND_Gate
  and and_4 (mulhu, ~Opcode_6, Opcode_5, Opcode_4, ~Opcode_3, ~Opcode_2, Opcode_1, Opcode_0, ~Funct3_2, Funct3_1, Funct3_0, ~Funct7_6, ~Funct7_5, ~Funct7_4, ~Funct7_3, ~Funct7_2, ~Funct7_1, Funct7_0);  // AND_Gate
  and and_5 (jal, Opcode_6, Opcode_5, ~Opcode_4, Opcode_3, Opcode_2, Opcode_1, Opcode_0);  // AND_Gate
  and and_6 (lui, ~Opcode_6, Opcode_5, Opcode_4, ~Opcode_3, Opcode_2, Opcode_1, Opcode_0);  // AND_Gate
  and and_7 (remu, ~Opcode_6, Opcode_5, Opcode_4, ~Opcode_3, ~Opcode_2, Opcode_1, Opcode_0, Funct3_2, Funct3_1, Funct3_0, ~Funct7_6, ~Funct7_5, ~Funct7_4, ~Funct7_3, ~Funct7_2, ~Funct7_1, Funct7_0);  // AND_Gate
  and and_8 (divu, ~Opcode_6, Opcode_5, Opcode_4, ~Opcode_3, ~Opcode_2, Opcode_1, Opcode_0, Funct3_2, ~Funct3_1, Funct3_0, ~Funct7_6, ~Funct7_5, ~Funct7_4, ~Funct7_3, ~Funct7_2, ~Funct7_1, Funct7_0);  // AND_Gate
  or or_1 (ALUSel_3, mul, sub, mulh, mulhu, divu, remu, lui, jal);
endmodule

module Template (
  input  in_1,
  input  in_2,
  input  in_3,
  input  in_4,
  input  in_5,
  input  in_6,
  input  in_7,
  input  in_8,
  input  in_9,
  input  in_10,
  input  in_11,
  input  in_12,
  input  in_13,
  input  in_14,
  input  in_15,
  input  in_16,
  input  in_17,
  input  in_18,
  input  in_19
);


  // Other names for the same wires on the sheet: BrEq = in_18; BrLt = in_19; Funct3_0 = in_10; Funct3_1 = in_9;
  //   Funct3_2 = in_8; Funct7_0 = in_17; Funct7_1 = in_16; Funct7_2 = in_15; Funct7_3 = in_14; Funct7_4 = in_13;
  //   Funct7_5 = in_12; Funct7_6 = in_11; Opcode_0 = in_7; Opcode_1 = in_6; Opcode_2 = in_5; Opcode_3 = in_4;
  //   Opcode_4 = in_3; Opcode_5 = in_2; Opcode_6 = in_1
endmodule
